# Fritzing sketch BME280-conncetion (saved by Fritzing 0.9.3b)

parts:
  Part1 = Arduino Uno (Rev3)
  M1 = BME280

nets:
  N1: Part1.A4/SDA, M1.SCL
  N2: Part1.A5/SCL, M1.SDA
  5V: Part1.5V, M1.VIN
  GND: Part1.GND, M1.GND

custom parts:
  BME280: Temperature Humidity Barometric presure Sensor

// code stored in the sketch: BME280BarometricSensorConnectionTest.ino
#include <Wire.h>
#include <SPI.h>
#include <Adafruit_Sensor.h>
#include <Adafruit_BME280.h>

Adafruit_BME280 bme; // I2C

void setup() {
    Serial.begin(9600);
    while(!Serial);    // time to get serial running
    Serial.println(F("BME280 test"));

    unsigned status;
    
    // default settings
    // (you can also pass in a Wire library object like &Wire2)
    status = bme.begin();  
    if (!status) {
        Serial.println("Could not find a valid BME280 sensor, check wiring, address, sensor ID!");
        Serial.print("SensorID was: 0x"); Serial.println(bme.sensorID(),16);
        Serial.print("        ID of 0xFF probably means a bad address, a BMP 180 or BMP 085\n");
        Serial.print("        ID of 0x56-0x58 represents a BMP 280,\n");
        Serial.print("        ID of 0x60 represents a BME 280.\n");
        Serial.print("        ID of 0x61 represents a BME 680.\n");
        while (1);
    }
    
    Serial.println("-- Default Test --");

    Serial.println();
}


void loop() { 
    Serial.print("Temperature = ");
    Serial.print(bme.readTemperature());
    Serial.println(" *C");

    Serial.print("Pressure = ");

    Serial.print(bme.readPressure() / 100.0F);
    Serial.println(" hPa");

    Serial.print("Humidity = ");
    Serial.print(bme.readHumidity());
    Serial.println(" %");

    Serial.println();
    delay(5000);
}

// code stored in the sketch: ESP8266WiFiModuleConnectionTest.ino
/**
 * ESP9266 WiFi Module Connection test
 */

#include <SoftwareSerial.h>

#define RX 10
#define TX 11

String WIFI_SSID     = "your-wifi-ssid";      // Your WiFi ssid
String WIFI_PASSWORD = "your-wifi-password";  // Password

SoftwareSerial esp8266(RX, TX);

void setup()
{  
  Serial.begin(9600);
  while (!Serial) {
    ; // wait for serial port to connect. Needed for native USB port only
  }
  
  Serial.println("ESP9266 WiFi Module Connection test");
  
  esp8266.begin(9600); //Baud rate for communicating with ESP8266. Your's might be different.
  delay(1000);
 
  esp8266Serial("AT", 1000);
  esp8266Serial("AT+GMR", 1000);
  esp8266Serial("AT+CWMODE=1", 1000); 
  esp8266Serial("AT+CIPMUX=1", 1000);
  esp8266Serial("AT+CWJAP=\"" + WIFI_SSID + "\",\"" + WIFI_PASSWORD + "\"", 10000);
  esp8266Serial("AT+CWJAP?", 1000);
  esp8266Serial("AT+CIFSR", 1000);
  esp8266Serial("AT+CIPSTATUS", 1000);
}

void loop() 
{
  Serial.println(millis());
  esp8266Serial("AT+CWJAP?", 1000);

  delay(10000);
}

String esp8266Serial(String command, const int timeout)
{
  Serial.print("ESP8266 command => ");
  Serial.println(command);
  
  String response = ""; // a String to hold incoming data
  esp8266.println(command);
  delay(50);
  long int time = millis();
  while ( (time + timeout) > millis())
  {
    while (esp8266.available())
    {
      response += esp8266.readString(); // Read the answer of ESP8266
    }   
  }

  Serial.print("ESP8266 response => ");
  Serial.println(response);   
  delay(200);

  return response;
}
